// Logisim project M20CS012_Q2.circ as structural Verilog: 1 circuit, main circuit main
module main (
  input  A,
  input  in_2,
  input  in_3,
  output out_4,
  output out_5
);

  wire nor_1_out, nor_2_out, nor_3_out, nor_4_out, nor_5_out, nor_6_out, nor_7_out;

  nor nor_1 (nor_1_out, A, in_2);
  nor nor_2 (nor_2_out, A, nor_1_out);
  nor nor_3 (nor_3_out, nor_1_out, in_2);
  nor nor_4 (nor_4_out, nor_2_out, nor_3_out);
  nor nor_5 (nor_5_out, nor_4_out, in_3);
  nor nor_6 (nor_6_out, nor_4_out, nor_5_out);
  nor nor_7 (nor_7_out, nor_5_out, in_3);
  nor nor_8 (out_4, nor_6_out, nor_7_out);
  nor nor_9 (out_5, nor_7_out, nor_3_out);

  // Notes on the sheet:
  //   B
  //   Borrow_in
  //   Borrow_out
  //   Difference
endmodule
