// Logisim project M20CS012_Q3.circ as structural Verilog: 1 circuit, main circuit main
module main (
  input  B,
  input  A,
  output Q0,
  output Q1,
  output Q2,
  output Q3
);

  wire not_1_out, not_2_out;

  not not_1 (not_1_out, B);
  not not_2 (not_2_out, A);
  and and_1 (Q0, not_1_out, not_2_out);
  and and_2 (Q1, B, not_2_out);
  and and_3 (Q2, not_1_out, A);
  and and_4 (Q3, A, B);
endmodule
